# Fritzing sketch BlastGate (saved by Fritzing 0.9.3b)
stripboards: 2

parts:
  Bauteil1 = Arduino Uno (Rev3)
  R1 = Resistor [tolerance=±5% resistance=10k package="2512 [SMD]"]
  R2 = Resistor [tolerance=±5% resistance=10k package="2512 [SMD]"]
  TRRS1 = Audio Jack (TRRS) 3.5mm [part_number="Audio Jack" package="RC-5325A [SMD]"]
  C1 = Electrolytic Capacitor [capacitance=10µF package="100 mil [THT, electrolytic]"]
  S2 = Momentary Switch [package=ksa_sealed_tac_switch]
  S4 = Momentary Switch [package=ksa_sealed_tac_switch]
  J2 = Basic Servo
  U1 = 2-Channel 5v Relay Shield [package=relay-2ch5v10a]
  LED2 = RGB LED (com. cathode, rbg) [package="5 mm [THT]"]
  R3 = Resistor [tolerance=±5% resistance=360 package="2512 [SMD]"]
  R4 = Resistor [tolerance=±5% resistance=220 package="2512 [SMD]"]
  R5 = Resistor [tolerance=±5% resistance=220 package="2512 [SMD]"]
  S5 = Momentary Switch [package=ksa_sealed_tac_switch]
  M1 = RioRand LM2596  # not connected
  M2 = RioRand LM2596

nets:
  N1: Bauteil1.A0, TRRS1.TIP
  N2: Bauteil1.D9_PWM, R3.Pin_0
  N3: Bauteil1.D10_PWM/SS, R4.Pin_0
  N4: Bauteil1.D11_PWM/MOSI, R5.Pin_0
  GND: Bauteil1.GND, R2.Pin_0, C1.-, S2.3, S4.3, U1.GND, LED2.common_cathode, S5.3, M2.Pin_4
  N5: Bauteil1.D2, S2.1
  N6: Bauteil1.D3_PWM, S4.1
  N7: Bauteil1.D4, S5.4
  N8: Bauteil1.D5_PWM, J2.pulse
  N9: Bauteil1.D6_PWM, U1.IN1
  5V: Bauteil1.5V, R1.Pin_0, U1.VCC
  N10: Bauteil1.VIN, M2.Pin_3
  N11: R1.Pin_1, R2.Pin_1, TRRS1.SLEEVE, C1.+
  N12: LED2.red_anode, R3.Pin_1
  N13: LED2.blue_anode, R4.Pin_1
  N14: LED2.green_anode, R5.Pin_1

notes:
  Servo connects to power directly and does not use aduinos power pin. Otherwise, a salling servo reboots arduino.
  This Buck Converter is set to 7.5 V to serve the arduino
  This one is set to 5.5V for the servo

custom parts:
  2-Channel 5v Relay Shield: 2 Channel 5v Relay Shield w. 2x SPD-06VDC-SD-C
